// Logisim project cvic.circ as structural Verilog: 2 circuits, main circuit main
module main (
  input  a,
  input  b,
  output out_3
);

  wire nand_1_out, nand_2_out, nand_3_out, nand_4_out, nand_5_out, nand_6_out, nand_7_out;

  nand nand_1 (nand_1_out, a, b);
  nand nand_2 (nand_2_out, a, a);
  nand nand_3 (nand_3_out, b, b);
  nand nand_4 (nand_4_out, nand_2_out, nand_3_out);
  nand nand_5 (nand_5_out, nand_1_out, nand_4_out);
  nand nand_6 (nand_6_out, nand_2_out, b);
  nand nand_7 (nand_7_out, nand_5_out, nand_5_out);
  nand nand_8 (out_3, nand_7_out, nand_6_out);
endmodule

module norka (
  input  a,
  input  b,
  output out_3
);

  wire nor_1_out, nor_2_out;

  nor nor_1 (nor_1_out, a, a);
  nor nor_2 (nor_2_out, nor_1_out, b);
  nor nor_3 (out_3, nor_2_out, nor_2_out);
endmodule
