// Logisim project ksi_circ.circ as structural Verilog: 4 circuits, main circuit first_bit
module example (
  input  A,
  input  B,
  input  CIn,
  output S,
  output COut
);

  wire and_1_out, and_2_out, and_3_out;

  xor xor_1 (S, A, B, CIn);
  and and_1 (and_1_out, A, B);
  and and_2 (and_2_out, A, CIn);
  and and_3 (and_3_out, B, CIn);
  or or_1 (COut, and_1_out, and_2_out, and_3_out);
endmodule

module first_bit (
  input  [15:0] A,
  output AnyOn,
  output [3:0] FstBit
);

  wire ABorCD_out, and_1_out, and_2_out, and_3_out, and_4_out, and_5_out, and_6_out, and_7_out, and_8_out,
       and_9_out, and_10_out, and_11_out, and_12_out, and_13_out, and_14_out, and_15_out, and_16_out,
       and_17_out, and_18_out, and_19_out, and_20_out, and_21_out, and_22_out, and_23_out, and_24_out,
       and_25_out, and_26_out, and_27_out, and_28_out, and_29_out, and_30_out, and_31_out, and_32_out,
       and_33_out, and_34_out, AorB_out, CorD_out, EForGH_out, EorF_out, GorH_out, not_1_out, not_2_out,
       not_3_out, not_4_out, not_5_out, not_6_out, not_7_out, not_8_out, not_9_out, not_10_out, not_11_out,
       not_12_out, not_13_out, not_14_out, or1or0_H_out, or3or2_G_out, or5or4_F_out, or7or6_E_out,
       or9or8_D_out, or11or10_C_out, or13or12_B_out, or15or14_A_out, or_2_out, or_3_out, or_5_out, or_6_out,
       or_7_out, or_8_out, or_9_out, or_10_out;

  and is_1xxx (FstBit[3], 1'b1, ABorCD_out);
  or AorB (AorB_out, or15or14_A_out, or13or12_B_out);
  or or15or14_A (or15or14_A_out, A[15], A[14]);
  or ABorCD (ABorCD_out, AorB_out, CorD_out);
  or or13or12_B (or13or12_B_out, A[13], A[12]);
  and and_1 (and_1_out, or15or14_A_out, FstBit[3]);
  not not_1 (not_1_out, FstBit[3]);
  not not_2 (not_2_out, FstBit[3]);
  or CorD (CorD_out, or11or10_C_out, or9or8_D_out);
  or or11or10_C (or11or10_C_out, A[11], A[10]);
  or or9or8_D (or9or8_D_out, A[9], A[8]);
  not not_3 (not_3_out, FstBit[3]);
  or finalOR (AnyOn, ABorCD_out, EForGH_out);
  and and_2 (and_2_out, EorF_out, not_3_out);
  and and_3 (and_3_out, AorB_out, FstBit[3]);
  and and_4 (and_4_out, or11or10_C_out, FstBit[3]);
  or EorF (EorF_out, or7or6_E_out, or5or4_F_out);
  or or7or6_E (or7or6_E_out, A[7], A[6]);
  or or5or4_F (or5or4_F_out, A[5], A[4]);
  or or_1 (FstBit[2], and_2_out, and_3_out);
  or EForGH (EForGH_out, EorF_out, GorH_out);
  or or3or2_G (or3or2_G_out, A[3], A[2]);
  and and_5 (and_5_out, or7or6_E_out, not_1_out);
  or GorH (GorH_out, or3or2_G_out, or1or0_H_out);
  or or1or0_H (or1or0_H_out, A[1], A[0]);
  not not_4 (not_4_out, FstBit[2]);
  and and_6 (and_6_out, or3or2_G_out, not_2_out);
  not not_5 (not_5_out, FstBit[2]);
  and and_7 (and_7_out, FstBit[2], and_1_out);
  and and_8 (and_8_out, not_5_out, and_4_out);
  and and_9 (and_9_out, and_5_out, FstBit[2]);
  and and_10 (and_10_out, and_6_out, not_4_out);
  or or_2 (or_2_out, and_7_out, and_8_out);
  or or_3 (or_3_out, and_9_out, and_10_out);
  or or_4 (FstBit[1], or_2_out, or_3_out);
  not not_6 (not_6_out, FstBit[3]);
  and and_11 (and_11_out, FstBit[3], A[15]);
  and and_12 (and_12_out, FstBit[3], A[13]);
  and and_13 (and_13_out, FstBit[3], A[11]);
  and and_14 (and_14_out, FstBit[3], A[9]);
  and and_15 (and_15_out, A[7], not_6_out);
  and and_16 (and_16_out, A[5], not_6_out);
  and and_17 (and_17_out, A[3], not_6_out);
  and and_18 (and_18_out, A[1], not_6_out);
  not not_7 (not_7_out, FstBit[2]);
  not not_8 (not_8_out, FstBit[2]);
  not not_9 (not_9_out, FstBit[2]);
  not not_10 (not_10_out, FstBit[2]);
  and and_19 (and_19_out, FstBit[2], and_11_out);
  and and_20 (and_20_out, FstBit[2], and_12_out);
  and and_21 (and_21_out, not_7_out, and_13_out);
  and and_22 (and_22_out, not_8_out, and_14_out);
  and and_23 (and_23_out, and_15_out, FstBit[2]);
  and and_24 (and_24_out, and_16_out, FstBit[2]);
  and and_25 (and_25_out, and_17_out, not_9_out);
  and and_26 (and_26_out, and_18_out, not_10_out);
  not not_11 (not_11_out, FstBit[1]);
  not not_12 (not_12_out, FstBit[1]);
  not not_13 (not_13_out, FstBit[1]);
  not not_14 (not_14_out, FstBit[1]);
  and and_27 (and_27_out, FstBit[1], and_19_out);
  and and_28 (and_28_out, not_11_out, and_20_out);
  and and_29 (and_29_out, FstBit[1], and_21_out);
  and and_30 (and_30_out, not_12_out, and_22_out);
  and and_31 (and_31_out, and_23_out, FstBit[1]);
  and and_32 (and_32_out, and_24_out, not_13_out);
  and and_33 (and_33_out, and_25_out, FstBit[1]);
  and and_34 (and_34_out, and_26_out, not_14_out);
  or or_5 (or_5_out, and_27_out, and_28_out);
  or or_6 (or_6_out, and_29_out, and_30_out);
  or or_7 (or_7_out, and_31_out, and_32_out);
  or or_8 (or_8_out, and_33_out, and_34_out);
  or or_9 (or_9_out, or_5_out, or_6_out);
  or or_10 (or_10_out, or_7_out, or_8_out);
  or or_11 (FstBit[0], or_9_out, or_10_out);
endmodule

module hamming_encode (
  input  [3:0] MIn,
  output [6:0] COut
);

  wire sum_p1_out, sum_p2_out, sum_p3_out;

  xor sum_p1 (sum_p1_out, MIn[3], MIn[2]);
  xor p1 (COut[6], sum_p1_out, MIn[0]);
  xor p2 (COut[5], sum_p2_out, MIn[0]);
  xor sum_p2 (sum_p2_out, MIn[3], MIn[1]);
  xor sum_p3 (sum_p3_out, MIn[2], MIn[1]);
  xor p3 (COut[3], sum_p3_out, MIn[0]);

  assign {COut[4], COut[2:0]} = MIn;
endmodule

module hamming_decode (
  input  [6:0] CIn,
  output [3:0] MOut,
  output Fault
);

  wire bit0_out, bit1_out, bit2_out, bit4_out, d2_xor_d4_out, d3_xor_d4_out, d3_xor_d_4_out, not_1_out,
       not_2_out, not_3_out, p1_odd_out, p1_xor_d1_out, p2_odd_out, p2_xor_d1_out, p3_odd_out, p3_xor_d2_out;

  xor p1_xor_d1 (p1_xor_d1_out, CIn[6], CIn[4]);
  xor d2_xor_d4 (d2_xor_d4_out, CIn[2], CIn[0]);
  xor p1_odd (p1_odd_out, p1_xor_d1_out, d2_xor_d4_out);
  xor p2_odd (p2_odd_out, p2_xor_d1_out, d3_xor_d_4_out);
  xor p2_xor_d1 (p2_xor_d1_out, CIn[5], CIn[4]);
  xor d3_xor_d_4 (d3_xor_d_4_out, CIn[1], CIn[0]);
  xor p3_xor_d2 (p3_xor_d2_out, CIn[3], CIn[2]);
  not not_1 (not_1_out, p2_odd_out);
  xor d3_xor_d4 (d3_xor_d4_out, CIn[1], CIn[0]);
  xor p3_odd (p3_odd_out, p3_xor_d2_out, d3_xor_d4_out);
  not not_2 (not_2_out, p1_odd_out);
  and bit2 (bit2_out, p3_odd_out, not_1_out, p1_odd_out);
  xor xor_1 (MOut[2], CIn[2], bit2_out);
  not not_3 (not_3_out, p3_odd_out);
  xor xor_2 (MOut[1], CIn[1], bit1_out);
  xor xor_3 (MOut[0], CIn[0], bit0_out);
  and bit1 (bit1_out, p2_odd_out, p3_odd_out, not_2_out);
  xor xor_4 (MOut[3], CIn[4], bit4_out);
  and bit4 (bit4_out, not_3_out, p1_odd_out, p2_odd_out);
  and bit0 (bit0_out, p2_odd_out, p3_odd_out, p1_odd_out);
  or is_bad (Fault, p2_odd_out, p3_odd_out, p1_odd_out);
endmodule
